// Logisim project a.circ as structural Verilog: 2 circuits, main circuit main
// aoeu
module main (
  input  in_1,
  input  in_2,
  output out_3
);

  Adder_part adder_1 ();  // open: a, b, out, cin, cout
  and and_1 (out_3, in_2, in_1);
  Adder adder_2 ();  // open: in_1, out_2
  Adder adder_3 ();  // open: in_1, out_2
endmodule

module Adder (
  input  in_1,
  output out_2
);
endmodule
